// Digital circuit RISC-V.dig as structural Verilog
module RISC_V (
  input  ON_OFF
);

  wire alu_1_c, and_1_out, decoder_1_done, decoder_1_error, decoder_1_instsubsubtype, fetcher_1_done,
       fetcher_1_oe, jmp_selector_1_nxt, lsu_1_c, lsu_1_c_ram, lsu_1_ld_ram, or_2_out, pc_1_done, rst;
  wire [2:0] decoder_1_instsubype;
  wire [3:0] decoder_1_insttype, decoder_1_jmptype;
  wire [4:0] alu_1_reg, decoder_1_inst, decoder_1_rd, decoder_1_rs1, decoder_1_shamt_rs2, lsu_1_reg, or_3_out;
  wire [7:0] lsu_1_din_ram, ramdualport_1_d, ROM_d;
  wire [23:0] fetcher_1_a, lsu_1_a_ram;
  wire [31:0] alu_1_d, decoder_1_imm, fetcher_1_val, jmp_selector_1_jmp_val, lsu_1_d, or_1_out, pc_1_addr,
       registers_1_rs1, registers_1_rs2;
  wire [31:24] lsu_1_a_ram_2;

  pulse #(.generic("Duration := 1;")) pulse_1 (.In(ON_OFF), .Out(rst));
  PC pc_1 (
    .Go(jmp_selector_1_nxt), .Rst(rst), .Nxt(jmp_selector_1_jmp_val), .Pwr(ON_OFF), .Addr(pc_1_addr),
    .Done(pc_1_done));
  fetcher fetcher_1 (
    .Addr(pc_1_addr), .C(pc_1_done), .Pwr(ON_OFF), .D(ROM_d), .Val(fetcher_1_val), .Done(fetcher_1_done),
    .A(fetcher_1_a), .OE(fetcher_1_oe));
  EEPROM #(.AddrBits(24), .isProgramMemory("true"), .Bits(8)) ROM (
    .A(fetcher_1_a), .CS(ON_OFF), .WE(1'b0), .OE(fetcher_1_oe), .D(ROM_d));
  decoder decoder_1 (
    .Val(fetcher_1_val), .C(fetcher_1_done), .Pwr(ON_OFF), .Done(decoder_1_done), .Error(decoder_1_error),
    .Inst(decoder_1_inst), .InstType(decoder_1_insttype), .InstSubype(decoder_1_instsubype),
    .InstSubSubType(decoder_1_instsubsubtype), .rd(decoder_1_rd), .rs1(decoder_1_rs1),
    .shamt_rs2(decoder_1_shamt_rs2), .imm(decoder_1_imm), .JmpType(decoder_1_jmptype));
  Break break_1 (.brk(decoder_1_done));
  Stop stop_1 (.stop(and_1_out));
  and and_1 (and_1_out, decoder_1_done, decoder_1_error);
  LSU lsu_1 (
    .D_RAM(ramdualport_1_d), .InstType(decoder_1_insttype), .InstSubType(decoder_1_instsubype),
    .imm(decoder_1_imm), .Pwr(ON_OFF), .rd(decoder_1_rd), .rs1_val_t_plus_1(registers_1_rs1),
    .rs2_val_t_plus_1(registers_1_rs2), .A_RAM({lsu_1_a_ram_2, lsu_1_a_ram}), .Din_RAM(lsu_1_din_ram),
    .C_RAM(lsu_1_c_ram), .ld_RAM(lsu_1_ld_ram), .Reg(lsu_1_reg), .D(lsu_1_d), .C(lsu_1_c));
  ALU alu_1 (
    .PC(pc_1_addr), .InstType(decoder_1_insttype), .InstSubType(decoder_1_instsubype),
    .InstSubSubType(decoder_1_instsubsubtype), .rd(decoder_1_rd), .imm(decoder_1_imm),
    .shamt(decoder_1_shamt_rs2), .rs1_val_t_plus_1(registers_1_rs1), .rs2_val_t_plus_1(registers_1_rs2),
    .Reg(alu_1_reg), .D(alu_1_d), .C(alu_1_c));
  registers registers_1 (
    .Reg(or_3_out), .D(or_1_out), .C(or_2_out), .rs1_sel(decoder_1_rs1), .rs2_sel(decoder_1_shamt_rs2),
    .Rst(rst), .Pwr(ON_OFF), .rs1(registers_1_rs1), .rs2(registers_1_rs2));
  jmp_selector jmp_selector_1 (
    .rs1_val_t_plus_1(registers_1_rs1), .rs2_val_t_plus_1(registers_1_rs2),
    .InstSubType(decoder_1_instsubype), .imm(decoder_1_imm), .JmpType(decoder_1_jmptype), .PC(pc_1_addr),
    .Nxt(jmp_selector_1_nxt), .Jmp_val(jmp_selector_1_jmp_val));
  RAMDualPort #(.AddrBits(24), .Bits(8)) ramdualport_1 (
    .A(lsu_1_a_ram), .Din(lsu_1_din_ram), .str(ON_OFF), .C(lsu_1_c_ram), .ld(lsu_1_ld_ram),
    .D(ramdualport_1_d));
  assign or_1_out = lsu_1_d | alu_1_d;  // Or or_1, 32 bits wide
  or or_2 (or_2_out, lsu_1_c, alu_1_c);
  assign or_3_out = lsu_1_reg | alu_1_reg;  // Or or_3, 5 bits wide

  // Other names for the same wires on the sheet: pwr = ON_OFF

  // Notes on the sheet:
  //   contents of ROM (hex, n*v repeats v):
  //   b7,10,0,0,13,d1,90,0,b3,d0,20,0,63,8,1,0,b3,81,30,0,13,1,f1,ff
  //   ,6f,f0,5f,ff,17,2,0,0,23,18,32
endmodule
