// Digital circuit fetcher.dig as structural Verilog
module fetcher (
  input  [31:0] Addr,
  input  C,
  input  Pwr,
  input  [7:0] D,
  output [31:0] Val,
  output Done,
  output [31:0] A,
  output OE
);

  wire delay_4_out, delay_5_out, delay_6_out, delay_7_out, delay_8_out, delay_9_out, delay_10_out,
       delay_11_out, delay_12_out, delay_13_out, delay_14_out, delay_15_out, delay_16_out, delay_17_out;
  wire [0:0] delay_1_out;
  wire [1:1] delay_2_out, delay_3_out;
  wire [31:0] or_1_out;

  Delay delay_1 (.in(C), .out(delay_1_out[0]));
  Delay #(.delayTime(3)) delay_2 (.in(C), .out(delay_2_out[1]));
  Delay #(.delayTime(5)) delay_3 (.in(C), .out(delay_3_out[1]));
  assign or_1_out = {32{1'b0}} | {{31{1'b0}}, delay_1_out[0]} | {{30{1'b0}}, delay_2_out[1], 1'b0} | {{30{1'b0}}, {2{delay_3_out[1]}}};  // Or or_1, 32 bits wide
  Delay delay_4 (.in(delay_1_out[0]), .out(delay_4_out));
  Delay delay_5 (.in(delay_2_out[1]), .out(delay_5_out));
  Delay delay_6 (.in(delay_3_out[1]), .out(delay_6_out));
  Delay delay_7 (.in(delay_1_out[0]), .out(delay_7_out));
  Delay delay_8 (.in(delay_2_out[1]), .out(delay_8_out));
  Delay delay_9 (.in(delay_3_out[1]), .out(delay_9_out));
  Add #(.Bits(32)) add_1 (.a(Addr), .b(or_1_out), .c_i(1'b0), .s(A));  // open: c_o
  or or_2 (OE, C, delay_4_out, delay_5_out, delay_6_out);
  Delay delay_10 (.in(C), .out(delay_10_out));
  Delay delay_11 (.in(delay_7_out), .out(delay_11_out));
  Delay delay_12 (.in(delay_8_out), .out(delay_12_out));
  Delay delay_13 (.in(delay_9_out), .out(delay_13_out));
  Delay delay_14 (.in(delay_10_out), .out(delay_14_out));
  Delay delay_15 (.in(delay_11_out), .out(delay_15_out));
  Delay delay_16 (.in(delay_12_out), .out(delay_16_out));
  Delay delay_17 (.in(delay_13_out), .out(delay_17_out));
  Register #(.Bits(8)) i0 (.D(D), .C(delay_14_out), .en(Pwr), .Q(Val[7:0]));
  Register #(.Bits(8)) i1 (.D(D), .C(delay_15_out), .en(Pwr), .Q(Val[15:8]));
  Register #(.Bits(8)) i2 (.D(D), .C(delay_16_out), .en(Pwr), .Q(Val[23:16]));
  Register #(.Bits(8)) i3 (.D(D), .C(delay_17_out), .en(Pwr), .Q(Val[31:24]));
  pulse #(.generic("Duration := 1;")) pulse_1 (.In(delay_17_out), .Out(Done));

  // Notes on the sheet:
  //   ROM
endmodule
